# Fritzing sketch greenhouse (saved by Fritzing 0.9.0b)
breadboards: 1

parts:
  Part1 = Arduino Mega 2560 (Rev3)
  R1 = Rotary Potentiometer (Small) [maximum_resistance=100kΩ package=THT]
  LCD1 = LCD screen
  R2 = Resistor [tolerance=±5% resistance=1k package=THT]
  S1 = Pushbutton [package="[THT]"]
  R3 = Resistor [tolerance=±5% resistance=1k package=THT]
  T1 = LM35 Temperature Sensor [thermistor_type=NTC package="TO92 [THT]"]
  R4 = Rotary Potentiometer (Small) [maximum_resistance=50Ω package=THT]
  VCC1 = Battery block 9V
  C1 = Electrolytic Capacitor [capacitance=1mF voltage=16V package="100 mil [THT, electrolytic]"]
  R5 = Resistor [tolerance=±5% resistance=220 package=THT]
  RHT1 = Humidity and Temperature Sensor RHT03
  R6 = Resistor [tolerance=±5% resistance=10k package=THT]
  J1 = Basic Servo

nets:
  N1: Part1.A0, T1.Vout
  N2: Part1.A1, R4.wiper
  N3: Part1.D14/TX3, J1.pulse
  GND: Part1.GND, R1.leg1, LCD1.VSS, LCD1.R/W, LCD1.LED-, R3.Pin_0, T1.GND, R4.leg2, VCC1.-, C1.-, C1.+, R5.Pin_0, RHT1.GND_2, J1.gnd
  N4: Part1.D13_PWM, RHT1.Data-signal, R6.Pin_0
  N5: Part1.D12_PWM, LCD1.RS
  N6: Part1.D11_PWM, LCD1.E
  N7: Part1.D8_PWM, S1.Pin_3, S1.Pin_4, R3.Pin_1
  5V: Part1.5V, R1.leg2, LCD1.VDD, R2.Pin_0, S1.Pin_1, S1.Pin_2, T1.+Vs, R4.leg1, RHT1.Vcc, R6.Pin_1
  N8: Part1.D2_PWM, LCD1.DB7
  N9: Part1.D3_PWM, LCD1.DB6
  N10: Part1.D4_PWM, LCD1.DB5
  N11: Part1.D5_PWM, LCD1.DB4
  N12: R1.wiper, LCD1.V0
  N13: LCD1.LED+, R2.Pin_1
  N14: VCC1.+, R5.Pin_1, J1.vcc
